// Digital circuit 4bitsToBcd.dig as structural Verilog
module _4bitsToBcd (
  input  [3:0] b,
  output [3:0] d,
  output [3:0] u
);

  wire comparator_1_eq, comparator_1_lt, or_1_out;
  wire [3:0] suma_resta_1_s_3;

  Comparator #(.Bits(4)) comparator_1 (
    .a(4'b0101), .b({1'b0, b[3:1]}), .eq(comparator_1_eq), .lt(comparator_1_lt));  // open: gt
  Suma_resta suma_resta_1 (
    .a_3(1'b0), .a_2(b[3]), .a_1(b[2]), .a_0(b[1]), .b_3(1'b0), .b_2(1'b0), .b_1(1'b1), .b_0(1'b1),
    .Op(1'b0), .s_3(suma_resta_1_s_3[3]), .s_2(suma_resta_1_s_3[2]), .s_1(suma_resta_1_s_3[1]),
    .s_0(suma_resta_1_s_3[0]));  // open: s_4
  Multiplexer #(.Bits(4)) multiplexer_1 (
    .sel(or_1_out), .in_0({1'b0, b[3:1]}), .in_1(suma_resta_1_s_3), .out({d[0], u[3:1]}));
  or or_1 (or_1_out, comparator_1_eq, comparator_1_lt);

  assign d[3:1] = 3'b000;
  assign u[0] = b[0];
endmodule
