// Digital circuit 7bitsToBcd.dig as structural Verilog
module _7bitsToBcd (
  input  [6:0] in_1,
  output [3:0] u,
  output [3:0] c,
  output [3:0] d
);

  wire [2:0] bitstobcd_1_d;
  wire [2:1] bitstobcd_1_d_2;
  wire [3:0] bitstobcd_3_d;
  wire [3:1] bitstobcd_2_d;

  bitsToBcd bitstobcd_1 (.b({1'b0, in_1[6:4]}), .d({bitstobcd_1_d_2[2], bitstobcd_1_d}));
  bitsToBcd bitstobcd_2 (.b({bitstobcd_1_d, in_1[3]}), .d({bitstobcd_1_d_2[1], bitstobcd_2_d}));
  bitsToBcd bitstobcd_3 (.b({bitstobcd_2_d, in_1[2]}), .d(bitstobcd_3_d));
  bitsToBcd bitstobcd_4 (.b({1'b0, bitstobcd_1_d_2, bitstobcd_3_d[3]}), .d({c[0], d[3:1]}));
  bitsToBcd bitstobcd_5 (.b({bitstobcd_3_d[2:0], in_1[1]}), .d({d[0], u[3:1]}));

  assign c[3:1] = 3'b000;
  assign u[0] = in_1[0];
endmodule
