// Digital circuit 9bitsToBcd.dig as structural Verilog
module _9bitsToBcd (
  input  [8:0] l,
  output [3:0] c,
  output [3:0] d,
  output [3:0] u
);

  wire [2:0] bitstobcd_3_d, bitstobcd_5_d, bitstobcd_7_d;
  wire [3:0] bitstobcd_1_d, bitstobcd_2_d, bitstobcd_4_d, bitstobcd_6_d, bitstobcd_8_d;

  bitsToBcd bitstobcd_1 (.b({1'b0, l[8:6]}), .d(bitstobcd_1_d));
  bitsToBcd bitstobcd_2 (.b({bitstobcd_1_d[2:0], l[5]}), .d(bitstobcd_2_d));
  bitsToBcd bitstobcd_3 (.b({2'b00, bitstobcd_1_d[3], bitstobcd_2_d[3]}), .d({c[3], bitstobcd_3_d}));
  bitsToBcd bitstobcd_4 (.b({bitstobcd_2_d[2:0], l[4]}), .d(bitstobcd_4_d));
  bitsToBcd bitstobcd_5 (.b({bitstobcd_3_d, bitstobcd_4_d[3]}), .d({c[2], bitstobcd_5_d}));
  bitsToBcd bitstobcd_6 (.b({bitstobcd_4_d[2:0], l[3]}), .d(bitstobcd_6_d));
  bitsToBcd bitstobcd_7 (.b({bitstobcd_5_d, bitstobcd_6_d[3]}), .d({c[1], bitstobcd_7_d}));
  bitsToBcd bitstobcd_8 (.b({bitstobcd_6_d[2:0], l[2]}), .d(bitstobcd_8_d));
  bitsToBcd bitstobcd_9 (.b({bitstobcd_7_d, bitstobcd_8_d[3]}), .d({c[0], d[3:1]}));
  bitsToBcd bitstobcd_10 (.b({bitstobcd_8_d[2:0], l[1]}), .d({d[0], u[3:1]}));

  assign u[0] = l[0];
endmodule
