// Digital circuit FFT.dig as structural Verilog
module FFT (
  input  cl,
  input  prst,
  output Q
);

  wire latchm_1_q, latchm_1_q_2, latchs_1_q_2, not_1_out;

  latchM latchm_1 (.r(Q), .s(latchs_1_q_2), .cl(cl), .Q(latchm_1_q), .Q_2(latchm_1_q_2));
  not not_1 (not_1_out, cl);
  latchS latchs_1 (.r(latchm_1_q_2), .s(latchm_1_q), .cl(not_1_out), .prst(prst), .Q(Q), .Q_2(latchs_1_q_2));
endmodule
