// Digital circuit Nollego.dig as structural Verilog
module Nollego (
  input  [8:0] l,
  output ov
);

  wire comparator_1_gt;

  Comparator #(.Bits(9)) comparator_1 (.a(l), .b(9'h8c), .gt(comparator_1_gt));  // open: eq, lt
  not not_1 (ov, comparator_1_gt);
endmodule
