// Digital circuit Suma_resta.dig as structural Verilog
module Suma_resta (
  input  a_3,
  input  a_2,
  input  a_1,
  input  a_0,
  input  b_3,
  input  b_2,
  input  b_1,
  input  b_0,
  input  Op,
  output s_4,
  output s_3,
  output s_2,
  output s_1,
  output s_0
);

  wire sumres_2_cbo, sumres_3_cbo, sumres_4_cbo;

  sumres sumres_1 (.op(Op), .a(a_3), .b(b_3), .cbi(sumres_2_cbo), .s(s_3), .cbo(s_4));
  sumres sumres_2 (.op(Op), .a(a_2), .b(b_2), .cbi(sumres_3_cbo), .s(s_2), .cbo(sumres_2_cbo));
  sumres sumres_3 (.op(Op), .a(a_1), .b(b_1), .cbi(sumres_4_cbo), .s(s_1), .cbo(sumres_3_cbo));
  sumres sumres_4 (.op(Op), .a(a_0), .b(b_0), .cbi(1'b0), .s(s_0), .cbo(sumres_4_cbo));

  // Notes on the sheet:
  //   testbech
endmodule
