// Digital circuit bitsToBcd (copia).dig as structural Verilog
module bitsToBcd__copia (
  input  [3:0] b,
  output d_0,
  output d_1,
  output d_2,
  output d_3
);

  wire comparator_1_eq, comparator_1_lt, or_1_out;
  wire [3:0] suma_resta_1_s_3;

  Suma_resta suma_resta_1 (
    .a_3(b[3]), .a_2(b[2]), .a_1(b[1]), .a_0(b[0]), .b_3(1'b0), .b_2(1'b0), .b_1(1'b1), .b_0(1'b1),
    .Op(1'b0), .s_3(suma_resta_1_s_3[3]), .s_2(suma_resta_1_s_3[2]), .s_1(suma_resta_1_s_3[1]),
    .s_0(suma_resta_1_s_3[0]));  // open: s_4
  Comparator #(.Bits(4)) comparator_1 (.a(4'b0101), .b(b), .eq(comparator_1_eq), .lt(comparator_1_lt));  // open: gt
  Multiplexer #(.Bits(4)) multiplexer_1 (.sel(or_1_out), .in_0(b), .in_1(suma_resta_1_s_3), .out({d_3, d_2, d_1, d_0}));
  or or_1 (or_1_out, comparator_1_eq, comparator_1_lt);
endmodule
