// Digital circuit cntr.dig as structural Verilog
module cntr (
  input  c,
  input  cl,
  output [19:0] cn
);

  wire not_1_out;

  not not_1 (not_1_out, c);
  Counter #(.Bits(20)) counter_1 (.en(c), .C(cl), .clr(not_1_out), .out(cn));  // open: ovf
endmodule
