// Digital circuit cntr9b.dig as structural Verilog
module cntr9b (
  input  c,
  input  cl,
  output [19:0] cn
);

  wire not_1_out;

  not not_1 (not_1_out, c);
  Counter #(.Bits(9)) counter_1 (.en(c), .C(cl), .clr(not_1_out), .out(cn[8:0]));  // open: ovf
  // Pins of 9 and 20 bits meet at cn
endmodule
