// Digital circuit counter.dig as structural Verilog
module counter (
  input  c,
  input  cl,
  output [19:0] t
);

  wire and_1_out, and_2_out, fft_1_q, fft_2_q, fft_3_q, fft_4_q, fft_5_q, fft_6_q, fft_7_q, fft_8_q, fft_9_q,
       fft_10_q, fft_11_q, fft_12_q, fft_13_q, fft_14_q, fft_15_q, fft_16_q, fft_17_q, fft_18_q, fft_19_q,
       fft_20_q, not_1_out, not_2_out, not_3_out, not_4_out, not_5_out, not_6_out, not_7_out, not_8_out,
       not_9_out, not_10_out, not_11_out, not_12_out, not_13_out, not_14_out, not_15_out, not_16_out,
       not_17_out, not_18_out, not_19_out, not_20_out, not_21_out, not_22_out;
  wire [19:0] and_10_out;

  Multiplexer #(.Bits(20)) multiplexer_1 (.sel(not_1_out), .in_0({20{1'b0}}), .in_1(and_10_out), .out(t));
  not not_1 (not_1_out, and_2_out);
  and and_1 (and_1_out, c, 1'b1);
  not not_2 (not_2_out, and_1_out);
  and and_2 (and_2_out, and_10_out[0], and_10_out[1], and_10_out[2], and_10_out[3], and_10_out[4], and_10_out[5], and_10_out[6], and_10_out[7], and_10_out[8], and_10_out[9], and_10_out[10], and_10_out[11], and_10_out[12], and_10_out[13], and_10_out[14], and_10_out[15], and_10_out[16], and_10_out[17], and_10_out[18], and_10_out[19]);
  and and_3 (and_10_out[0], not_3_out, fft_1_q);
  not not_3 (not_3_out, not_2_out);
  FFT fft_1 (.cl(cl), .prst(not_2_out), .Q(fft_1_q));
  and and_4 (and_10_out[1], not_4_out, fft_2_q);
  not not_4 (not_4_out, not_2_out);
  FFT fft_2 (.cl(fft_1_q), .prst(not_2_out), .Q(fft_2_q));
  FFT fft_3 (.cl(fft_2_q), .prst(not_2_out), .Q(fft_3_q));
  and and_5 (and_10_out[2], not_5_out, fft_3_q);
  not not_5 (not_5_out, not_2_out);
  FFT fft_4 (.cl(fft_3_q), .prst(not_2_out), .Q(fft_4_q));
  and and_6 (and_10_out[3], not_6_out, fft_4_q);
  not not_6 (not_6_out, not_2_out);
  and and_7 (and_10_out[4], not_7_out, fft_5_q);
  not not_7 (not_7_out, not_2_out);
  FFT fft_5 (.cl(fft_4_q), .prst(not_2_out), .Q(fft_5_q));
  and and_8 (and_10_out[5], not_8_out, fft_6_q);
  not not_8 (not_8_out, not_2_out);
  FFT fft_6 (.cl(fft_5_q), .prst(not_2_out), .Q(fft_6_q));
  FFT fft_7 (.cl(fft_6_q), .prst(not_2_out), .Q(fft_7_q));
  and and_9 (and_10_out[6], not_9_out, fft_7_q);
  not not_9 (not_9_out, not_2_out);
  FFT fft_8 (.cl(fft_7_q), .prst(not_2_out), .Q(fft_8_q));
  and and_10 (and_10_out[7], not_10_out, fft_8_q);
  not not_10 (not_10_out, not_2_out);
  and and_11 (and_10_out[8], not_11_out, fft_9_q);
  not not_11 (not_11_out, not_2_out);
  FFT fft_9 (.cl(fft_8_q), .prst(not_2_out), .Q(fft_9_q));
  and and_12 (and_10_out[9], not_12_out, fft_10_q);
  not not_12 (not_12_out, not_2_out);
  FFT fft_10 (.cl(fft_9_q), .prst(not_2_out), .Q(fft_10_q));
  FFT fft_11 (.cl(fft_10_q), .prst(not_2_out), .Q(fft_11_q));
  and and_13 (and_10_out[10], not_13_out, fft_11_q);
  not not_13 (not_13_out, not_2_out);
  FFT fft_12 (.cl(fft_11_q), .prst(not_2_out), .Q(fft_12_q));
  and and_14 (and_10_out[11], not_14_out, fft_12_q);
  not not_14 (not_14_out, not_2_out);
  and and_15 (and_10_out[12], not_15_out, fft_13_q);
  not not_15 (not_15_out, not_2_out);
  FFT fft_13 (.cl(fft_12_q), .prst(not_2_out), .Q(fft_13_q));
  and and_16 (and_10_out[13], not_16_out, fft_14_q);
  not not_16 (not_16_out, not_2_out);
  FFT fft_14 (.cl(fft_13_q), .prst(not_2_out), .Q(fft_14_q));
  FFT fft_15 (.cl(fft_14_q), .prst(not_2_out), .Q(fft_15_q));
  and and_17 (and_10_out[14], not_17_out, fft_15_q);
  not not_17 (not_17_out, not_2_out);
  FFT fft_16 (.cl(fft_15_q), .prst(not_2_out), .Q(fft_16_q));
  and and_18 (and_10_out[15], not_18_out, fft_16_q);
  not not_18 (not_18_out, not_2_out);
  and and_19 (and_10_out[16], not_19_out, fft_17_q);
  not not_19 (not_19_out, not_2_out);
  FFT fft_17 (.cl(fft_16_q), .prst(not_2_out), .Q(fft_17_q));
  and and_20 (and_10_out[17], not_20_out, fft_18_q);
  not not_20 (not_20_out, not_2_out);
  FFT fft_18 (.cl(fft_17_q), .prst(not_2_out), .Q(fft_18_q));
  FFT fft_19 (.cl(fft_18_q), .prst(not_2_out), .Q(fft_19_q));
  and and_21 (and_10_out[18], not_21_out, fft_19_q);
  not not_21 (not_21_out, not_2_out);
  FFT fft_20 (.cl(fft_19_q), .prst(not_2_out), .Q(fft_20_q));
  and and_22 (and_10_out[19], not_22_out, fft_20_q);
  not not_22 (not_22_out, not_2_out);

  // Notes on the sheet:
  //   cl: Hz: 10
endmodule
