// Digital circuit distancia.dig as structural Verilog
module distancia (
  input  [19:0] cn,
  output [8:0] may
);

  wire [39:0] mul_1_mul;

  Mul #(.Bits(20)) mul_1 (.a(20'h167), .b(cn), .mul({mul_1_mul[39:29], may, mul_1_mul[19:0]}));
  // Pins of 1 and 9 bits meet at may
endmodule
