// Digital circuit div_f.dig as structural Verilog
module div_f (
  input  F_in,
  output F_out
);

  wire t_ff_1_q, t_ff_2_q, t_ff_3_q, t_ff_4_q, t_ff_5_q, t_ff_6_q, t_ff_7_q, t_ff_8_q, t_ff_9_q, t_ff_10_q,
       t_ff_11_q, t_ff_12_q, t_ff_13_q, t_ff_14_q, t_ff_15_q;

  T_FF t_ff_1 (.T(1'b1), .C(F_in), .Q(t_ff_1_q));  // open: nQ
  T_FF t_ff_2 (.T(1'b1), .C(t_ff_1_q), .Q(t_ff_2_q));  // open: nQ
  T_FF t_ff_3 (.T(1'b1), .C(t_ff_2_q), .Q(t_ff_3_q));  // open: nQ
  T_FF t_ff_4 (.T(1'b1), .C(t_ff_3_q), .Q(t_ff_4_q));  // open: nQ
  T_FF t_ff_5 (.T(1'b1), .C(t_ff_4_q), .Q(t_ff_5_q));  // open: nQ
  T_FF t_ff_6 (.T(1'b1), .C(t_ff_5_q), .Q(t_ff_6_q));  // open: nQ
  T_FF t_ff_7 (.T(1'b1), .C(t_ff_6_q), .Q(t_ff_7_q));  // open: nQ
  T_FF t_ff_8 (.T(1'b1), .C(t_ff_7_q), .Q(t_ff_8_q));  // open: nQ
  T_FF t_ff_9 (.T(1'b1), .C(t_ff_8_q), .Q(t_ff_9_q));  // open: nQ
  T_FF t_ff_10 (.T(1'b1), .C(t_ff_9_q), .Q(t_ff_10_q));  // open: nQ
  T_FF t_ff_11 (.T(1'b1), .C(t_ff_10_q), .Q(t_ff_11_q));  // open: nQ
  T_FF t_ff_12 (.T(1'b1), .C(t_ff_11_q), .Q(t_ff_12_q));  // open: nQ
  T_FF t_ff_13 (.T(1'b1), .C(t_ff_12_q), .Q(t_ff_13_q));  // open: nQ
  T_FF t_ff_14 (.T(1'b1), .C(t_ff_13_q), .Q(t_ff_14_q));  // open: nQ
  T_FF t_ff_15 (.T(1'b1), .C(t_ff_14_q), .Q(t_ff_15_q));  // open: nQ
  T_FF t_ff_16 (.T(1'b1), .C(t_ff_15_q), .Q(F_out));  // open: nQ
endmodule
