// Digital circuit divff.dig as structural Verilog
module divff (
  input  cl,
  output clf
);

  wire d_ff_1_nq, d_ff_1_q, d_ff_2_nq, d_ff_2_q, d_ff_3_nq, d_ff_3_q, d_ff_4_nq, d_ff_4_q, d_ff_5_nq,
       d_ff_5_q, d_ff_6_nq, d_ff_6_q, d_ff_7_nq, d_ff_7_q, d_ff_8_nq, d_ff_9_nq, d_ff_9_q, d_ff_10_nq,
       d_ff_10_q, d_ff_11_nq, d_ff_11_q, d_ff_12_nq, d_ff_12_q, d_ff_13_nq, d_ff_13_q;

  D_FF d_ff_1 (.D(d_ff_1_nq), .C(cl), .Q(d_ff_1_q), .nQ(d_ff_1_nq));
  D_FF d_ff_2 (.D(d_ff_2_nq), .C(d_ff_13_q), .Q(d_ff_2_q), .nQ(d_ff_2_nq));
  D_FF d_ff_3 (.D(d_ff_3_nq), .C(d_ff_1_q), .Q(d_ff_3_q), .nQ(d_ff_3_nq));
  D_FF d_ff_4 (.D(d_ff_4_nq), .C(d_ff_2_q), .Q(d_ff_4_q), .nQ(d_ff_4_nq));
  D_FF d_ff_5 (.D(d_ff_5_nq), .C(d_ff_3_q), .Q(d_ff_5_q), .nQ(d_ff_5_nq));
  D_FF d_ff_6 (.D(d_ff_6_nq), .C(d_ff_4_q), .Q(d_ff_6_q), .nQ(d_ff_6_nq));
  D_FF d_ff_7 (.D(d_ff_7_nq), .C(d_ff_5_q), .Q(d_ff_7_q), .nQ(d_ff_7_nq));
  D_FF d_ff_8 (.D(d_ff_8_nq), .C(d_ff_6_q), .Q(clf), .nQ(d_ff_8_nq));
  D_FF d_ff_9 (.D(d_ff_9_nq), .C(d_ff_7_q), .Q(d_ff_9_q), .nQ(d_ff_9_nq));
  D_FF d_ff_10 (.D(d_ff_10_nq), .C(d_ff_9_q), .Q(d_ff_10_q), .nQ(d_ff_10_nq));
  D_FF d_ff_11 (.D(d_ff_11_nq), .C(d_ff_10_q), .Q(d_ff_11_q), .nQ(d_ff_11_nq));
  D_FF d_ff_12 (.D(d_ff_12_nq), .C(d_ff_11_q), .Q(d_ff_12_q), .nQ(d_ff_12_nq));
  D_FF d_ff_13 (.D(d_ff_13_nq), .C(d_ff_12_q), .Q(d_ff_13_q), .nQ(d_ff_13_nq));
endmodule
