// Digital circuit eq.dig as structural Verilog
module eq (
  input  [3:0] bc,
  output eq
);

  wire comparator_1_eq;

  Comparator #(.Bits(4)) comparator_1 (.a(4'b0000), .b(bc), .eq(comparator_1_eq));  // open: gt, lt
  not not_1 (eq, comparator_1_eq);
endmodule
