// Digital circuit fraccion.dig as structural Verilog
module fraccion (
  input  [3:0] b,
  output [3:0] d
);

  wire and_2_out, and_3_out, and_4_out, and_5_out, and_6_out, and_7_out, and_8_out, and_9_out, and_10_out,
       and_11_out, and_12_out, and_13_out, not_1_out, not_2_out, not_3_out, not_4_out;

  not not_1 (not_1_out, b[3]);
  not not_2 (not_2_out, b[2]);
  not not_3 (not_3_out, b[1]);
  not not_4 (not_4_out, b[0]);
  and and_1 (d[3], b[2], b[3]);
  and and_2 (and_2_out, b[1], b[2], not_1_out);
  and and_3 (and_3_out, not_2_out, b[3]);
  and and_4 (and_4_out, b[0], b[1], not_2_out);
  and and_5 (and_5_out, b[0], not_2_out, b[3]);
  and and_6 (and_6_out, not_3_out, b[2], not_1_out);
  and and_7 (and_7_out, b[1], not_2_out, b[3]);
  and and_8 (and_8_out, b[0], not_3_out, not_1_out);
  and and_9 (and_9_out, not_4_out, b[1], not_2_out);
  and and_10 (and_10_out, b[0], b[2]);
  and and_11 (and_11_out, not_4_out, not_2_out, b[3]);
  and and_12 (and_12_out, not_3_out, b[2], not_1_out);
  and and_13 (and_13_out, b[1], b[3]);
  or or_1 (d[2], and_2_out, and_3_out);
  or or_2 (d[1], and_4_out, and_5_out, and_6_out, and_7_out);
  or or_3 (d[0], and_8_out, and_9_out, and_10_out, and_11_out, and_12_out, and_13_out);

  // Other names for the same wires on the sheet: b_0 = b[0]; b_1 = b[1]; b_2 = b[2]; b_3 = b[3]; d_0 = d[0];
  //   d_1 = d[1]; d_2 = d[2]; d_3 = d[3]
endmodule
