// Digital circuit latchS.dig as structural Verilog
module latchS (
  input  r,
  input  s,
  input  cl,
  input  prst,
  output Q,
  output Q_2
);

  wire and_1_out, and_2_out, or_1_out, or_2_out;

  and and_1 (and_1_out, r, cl);
  and and_2 (and_2_out, s, cl);
  or or_1 (or_1_out, Q_2, and_1_out);
  or or_2 (or_2_out, and_2_out, prst, Q);
  not not_1 (Q, or_1_out);
  not not_2 (Q_2, or_2_out);
endmodule
