// Digital circuit prueba_7seg.dig as structural Verilog
module prueba_7seg (
  input  clk
);

  wire A, B, C, D, E, F, G, not_1_out;
  wire [3:0] counter_1_out;

  not not_1 (not_1_out, 1'b0);
  Counter #(.Bits(4)) counter_1 (.en(not_1_out), .C(clk), .clr(1'b0), .out(counter_1_out));  // open: ovf
  seg7 seg7_1 (.e(counter_1_out), .s({G, F, E, D, C, B, A}));
  Seven_Seg #(.commonCathode("true"), .commonConnectionType("anode")) seven_seg_1 (
    .a(A), .b(B), .c(C), .d(D), .e(E), .f(F), .g(G), .dp(1'b1), .common(1'b1));
endmodule
