// Digital circuit prueba_sensor.dig as structural Verilog
module prueba_sensor (
  input  clk,
  output [8:0] d,
  output T
);

  wire A, B, C, D_t, E, F, G, H, L_1, L_2, L_3, L_4;

  // sensor sensor_1: pin names not known; wires that end beside it: clk, T, L_4, L_3, L_2, L_1, A, B, C, D_t, E, F, G, H, d
  Seven_Seg #(.commonCathode("true"), .commonConnectionType("anode"), .persistTime(100)) seven_seg_1 (
    .a(A), .b(B), .c(C), .d(D_t), .e(E), .f(F), .g(G), .dp(H), .common(L_4));
  Seven_Seg #(.commonCathode("true"), .commonConnectionType("anode"), .persistTime(100)) seven_seg_2 (
    .a(A), .b(B), .c(C), .d(D_t), .e(E), .f(F), .g(G), .dp(H), .common(L_3));
  Seven_Seg #(.commonCathode("true"), .commonConnectionType("anode"), .persistTime(100)) seven_seg_3 (
    .a(A), .b(B), .c(C), .d(D_t), .e(E), .f(F), .g(G), .dp(H), .common(L_2));
  Seven_Seg #(.commonCathode("true"), .commonConnectionType("anode"), .persistTime(100)) seven_seg_4 (
    .a(A), .b(B), .c(C), .d(D_t), .e(E), .f(F), .g(G), .dp(H), .common(L_1));

  // Notes on the sheet:
  //   clk: Hz: 25000000
endmodule
