// Digital circuit relojC.dig as structural Verilog
module relojC (
  input  cl,
  output [19:0] cn
);

  wire not_1_out;

  not not_1 (not_1_out, 1'b1);
  Counter #(.Bits(20)) counter_1 (.en(1'b1), .C(cl), .clr(not_1_out), .out(cn));  // open: ovf
endmodule
