// Digital circuit seg72.dig as structural Verilog
module seg72 (
  input  [3:0] e,
  output [6:0] s
);

  wire and_1_out, and_2_out, and_3_out, and_4_out, and_5_out, and_6_out, and_7_out, and_8_out, and_9_out,
       and_10_out, and_11_out, and_12_out, and_13_out, and_14_out, and_15_out, and_16_out, and_17_out,
       and_18_out, and_19_out, and_20_out, and_21_out, and_22_out, and_23_out, and_24_out, and_25_out,
       and_26_out, not_1_out, not_2_out, not_3_out, not_4_out;

  not not_1 (not_1_out, e[3]);
  not not_2 (not_2_out, e[2]);
  not not_3 (not_3_out, e[1]);
  not not_4 (not_4_out, e[0]);
  and and_1 (and_1_out, e[0], not_3_out, not_2_out, not_1_out);
  and and_2 (and_2_out, not_4_out, not_3_out, e[2]);
  and and_3 (and_3_out, not_4_out, e[2], e[3]);
  and and_4 (and_4_out, e[0], not_3_out, e[2]);
  and and_5 (and_5_out, not_4_out, e[1], e[2]);
  and and_6 (and_6_out, not_4_out, e[1], e[3]);
  and and_7 (and_7_out, not_4_out, e[2], e[3]);
  and and_8 (and_8_out, not_4_out, e[1], not_2_out);
  and and_9 (and_9_out, not_4_out, e[1], e[3]);
  and and_10 (and_10_out, not_3_out, e[2], e[3]);
  and and_11 (and_11_out, e[0], not_3_out, not_2_out);
  and and_12 (and_12_out, not_4_out, not_3_out, e[2], not_1_out);
  and and_13 (and_13_out, e[0], e[1], e[2], not_1_out);
  and and_14 (and_14_out, not_4_out, e[1], e[3]);
  and and_15 (and_15_out, e[0], not_2_out, e[3]);
  and and_16 (and_16_out, e[0], not_1_out);
  and and_17 (and_17_out, e[0], not_3_out, not_2_out);
  and and_18 (and_18_out, not_4_out, e[1], e[2], e[3]);
  and and_19 (and_19_out, not_3_out, e[2], not_1_out);
  and and_20 (and_20_out, e[0], not_2_out, not_1_out);
  and and_21 (and_21_out, e[0], e[1], not_1_out);
  and and_22 (and_22_out, not_4_out, e[1], e[2], e[3]);
  and and_23 (and_23_out, e[1], not_2_out, not_1_out);
  and and_24 (and_24_out, e[0], e[1], e[2]);
  and and_25 (and_25_out, not_3_out, not_2_out, not_1_out);
  and and_26 (and_26_out, e[2], e[3]);
  or or_1 (s[6], and_1_out, and_2_out, and_3_out);
  or or_2 (s[4], and_8_out, and_9_out, and_10_out);
  or or_3 (s[0], and_24_out, and_25_out, and_26_out);
  or or_4 (s[5], and_4_out, and_5_out, and_6_out, and_7_out);
  or or_5 (s[3], and_11_out, and_12_out, and_13_out, and_14_out, and_15_out);
  or or_6 (s[2], and_16_out, and_17_out, and_18_out, and_19_out);
  or or_7 (s[1], and_20_out, and_21_out, and_22_out, and_23_out);

  // Other names for the same wires on the sheet: e_0 = e[0]; e_1 = e[1]; e_2 = e[2]; e_3 = e[3]; s_0 = s[0];
  //   s_1 = s[1]; s_2 = s[2]; s_3 = s[3]; s_4 = s[4]; s_5 = s[5]; s_6 = s[6]
endmodule
