// Digital circuit sensor.dig as structural Verilog
module sensor (
  input  cl,
  input  ec,
  output trig,
  output Max,
  output Min
);

  wire [19:0] cntr_1_cn, relojc_1_cn;

  relojC relojc_1 (.cl(cl), .cn(relojc_1_cn));
  cntr cntr_1 (.c(ec), .cl(cl), .cn(cntr_1_cn));
  tpulso tpulso_1 (.l(relojc_1_cn), .ov(trig));
  Comparator #(.Bits(20)) comparator_1 (.a(cntr_1_cn), .b(20'h155a8), .gt(Max));  // open: eq, lt
  Comparator #(.Bits(20)) comparator_2 (.a(cntr_1_cn), .b(20'he3c5), .lt(Min));  // open: gt, eq

  // Notes on the sheet:
  //   cl: Hz: 50000
endmodule
