// Digital circuit sumres.dig as structural Verilog
module sumres (
  input  op,
  input  a,
  input  b,
  input  cbi,
  output s,
  output cbo
);

  wire and_1_out, and_2_out, and_3_out, and_4_out, and_5_out, and_6_out, and_7_out, and_8_out, and_9_out,
       not_1_out, not_2_out, not_3_out, not_4_out;

  not not_1 (not_1_out, op);
  not not_2 (not_2_out, a);
  not not_3 (not_3_out, b);
  not not_4 (not_4_out, cbi);
  and and_1 (and_1_out, not_2_out, not_3_out, cbi);
  and and_2 (and_2_out, not_2_out, b, not_4_out);
  and and_3 (and_3_out, a, not_3_out, not_4_out);
  and and_4 (and_4_out, a, b, cbi);
  and and_5 (and_5_out, a, cbi, not_1_out);
  and and_6 (and_6_out, a, b, not_1_out);
  and and_7 (and_7_out, not_2_out, cbi, op);
  and and_8 (and_8_out, not_2_out, b, op);
  and and_9 (and_9_out, b, cbi);
  or or_1 (s, and_1_out, and_2_out, and_3_out, and_4_out);
  or or_2 (cbo, and_5_out, and_6_out, and_7_out, and_8_out, and_9_out);
endmodule
