// Digital circuit tpulso.dig as structural Verilog
module tpulso (
  input  [19:0] l,
  output ov
);

  wire comparator_1_gt;

  Comparator #(.Bits(20)) comparator_1 (.a(l), .b(20'h1f4), .gt(comparator_1_gt));  // open: eq, lt
  not not_1 (ov, comparator_1_gt);
endmodule
